# Fritzing sketch Servo example (saved by Fritzing 0.9.2b)
breadboards: 1

parts:
  J1 = Basic Servo
  Part1 = Arduino Uno (Rev3)
  R1 = Rotary Potentiometer (Small) [maximum_resistance=100kΩ package=THT]

nets:
  VCC: J1.vcc, Part1.5V, R1.leg2
  N1: J1.pulse, Part1.D9_PWM
  N2: Part1.A0, R1.wiper
  N3: Part1.GND, R1.leg1

notes:
  not shure about the Pot left gnd or right gnd ... Somethings I just froget.
